# Fritzing sketch circuit (saved by Fritzing 0.8.7b)
breadboards: 1

parts:
  Part1 = Arduino Nano (Rev3.0)
  IC1 = L293D [package=THT]
  IC2 = L293D [package=THT]
  BAT1 = BC9VPC [package=bc9vpc]
  BAT2 = BC9VPC [package=bc9vpc]
  M1 = DC Motor
  M2 = DC Motor
  M3 = DC Motor
  R1 = PHOTOCELL [package=photocell-kit]
  R2 = PHOTOCELL [package=photocell-kit]
  R3 = PHOTOCELL [package=photocell-kit]

nets:
  N1: Part1.GND, IC1.0V, IC2.0V, BAT2.V+
  N2: Part1.D3, IC1.In_4
  N3: Part1.D5, IC1.In_1
  N4: Part1.D6, IC2.In_1
  N5: Part1.D9, IC1.In_3
  N6: Part1.D10, IC1.In_2
  N7: Part1.D11/MOSI, IC2.In_2
  N8: Part1.5V, IC1.+V, IC2.+V, R1.P$2, R2.P$1, R3.P$2
  N9: Part1.A3, R2.P$2
  N10: Part1.A2, R3.P$1
  N11: Part1.A0, R1.P$1
  N12: IC1.Out_1_(_Controlled_by_Enable_1_), M2.pin_2
  N13: IC1.Out_2_(_Controlled_by_Enable_1_), M2.pin_1
  N14: IC1.+Vmotor, IC1.Enable_2, IC2.+Vmotor, BAT1.V-
  N15: IC1.Out_3_(_Controlled_by_Enable_2_), M1.pin_2
  N16: IC1.Out_4_(_Controlled_by_Enable_2_), M1.pin_1
  N17: IC2.Out_1_(_Controlled_by_Enable_1_), M3.pin_1
  N18: IC2.Out_2_(_Controlled_by_Enable_1_), M3.pin_2
  N19: BAT1.V+, BAT2.V-
